# Fritzing sketch Photoresistor (saved by Fritzing 0.9.6b)
breadboards: 1

parts:
  R1 = Photocell (LDR) [package=THT]
  R2 = Resistor [tolerance=±5% power=0.25 resistance=1k package=THT]
  Componente1 = Arduino Uno (Rev3)

nets:
  N1: R1.pin_0, Componente1.3V3
  N2: R1.pin_1, R2.Pin_0, Componente1.A0
  N3: R2.Pin_1, Componente1.GND
