# Fritzing sketch twitter_monoled (saved by Fritzing 0.9.6b)
breadboards: 1

parts:
  LED2 = RGB LED (com. cathode, rgb) [package="5 mm [THT]"]
  U1 = ESP8266 NodeMCU LoLin module
  R4 = Resistor [tolerance=±5% power=0.25 resistance=220 package=THT]
  R5 = Resistor [tolerance=±5% power=0.25 resistance=220 package=THT]
  R6 = Resistor [tolerance=±5% power=0.25 resistance=220 package=THT]

nets:
  N1: LED2.red_anode, R4.Pin_0
  N2: LED2.common_cathode, U1.3V3
  N3: LED2.green_anode, R5.Pin_0
  N4: LED2.blue_anode, R6.Pin_0
  N5: U1.D0, R4.Pin_1
  N6: U1.D2, R5.Pin_1
  N7: U1.D3, R6.Pin_1

custom parts:
  ESP8266 NodeMCU LoLin module: ESP8266 based NodeMCU
